# Fritzing sketch sketch (saved by Fritzing 0.9.2b)
breadboards: 1

parts:
  A1 = WeMos D1 R1
  U1 = 74HC4051 [package=so16]
  U2 = GAS_SENSOR [package=mq-3]
  J1 = Basic Servo
  M1 = ph-4502c [package=THT]

nets:
  VDD: A1.Pin_9, U1.VDD, U2.H2, J1.vcc, M1.pin6
  VSS: A1.Pin_11, A1.Pin_32, A1.Pin_36, U1.INH, U1.VEE, U1.VSS, U2.H1, J1.gnd, M1.pin4, M1.pin5
  N1: A1.Pin_17, U1.IO
  N2: A1.Pin_48, U1.A
  N3: A1.Pin_50, U1.B
  N4: A1.Pin_52, A1.Pin_63, U1.C
  N5: A1.Pin_54, J1.pulse
  N6: U1.IO0, U2.B1
  N7: U1.IO1, M1.pin3
  N8: U1.IO2, M1.pin1

custom parts:
  WeMos D1 R1: The WeMos D1 is a ESP8266 WiFi based board that uses the Arduino layout with a operating voltage of 3.3V.
  ph-4502c: ph-4502c PH Meter.
